# Fritzing sketch digital_temperature (saved by Fritzing 0.9.4)
circuit board: 8.46667cm x 5.64444cm
breadboards: 1

parts:
  BY-028_temperature = KY-028 Digital Temperature Sensor Module [package="Breakout board"]
  arduino_uno_r3 = Arduino Uno (Rev3)
  Green_led = smd LED [color="Green (565nm)" package="1206 [SMD]"]
  Red_led = smd LED [color="Red (633nm)" package="1206 [SMD]"]
  R1 = Resistor [tolerance=±5% resistance=220 package="1206 [SMD]"]
  R2 = Resistor [tolerance=±5% resistance=220 package="1206 [SMD]"]

nets:
  N1: BY-028_temperature.A0, arduino_uno_r3.A0
  N2: BY-028_temperature.G, arduino_uno_r3.GND, Green_led.anode, Red_led.anode
  N3: BY-028_temperature.+, arduino_uno_r3.5V
  N4: BY-028_temperature.D0, arduino_uno_r3.D2
  N5: arduino_uno_r3.D8, Green_led.cathode, R2.Pin_0, R2.Pin_1
  N6: arduino_uno_r3.D12/MISO, Red_led.cathode, R1.Pin_0, R1.Pin_1

notes:
  richistron.com

custom parts:
  KY-028 Digital Temperature Sensor Module: KEYES KY-028 Digital Temperature Sensor Module, used to measure changes in temperature.
