# Fritzing sketch digitablueprints (saved by Fritzing 0.9.4)
breadboards: 1

parts:
  Part1 = KY-028 Digital Temperature Sensor Module [package="Breakout board"]
  Part2 = Arduino Uno (Rev3)
  LED1 = smd LED [color="Green (565nm)" package="1206 [SMD]"]
  LED2 = smd LED [color="Yellow (595nm)" package="1206 [SMD]"]
  LED3 = smd LED [color="Red (633nm)" package="1206 [SMD]"]

nets:
  N1: Part1.A0, Part2.A0
  N2: Part1.G, Part2.GND, LED1.cathode, LED2.cathode, LED3.cathode
  N3: Part1.+, Part2.5V
  N4: Part1.D0, Part2.D2

custom parts:
  KY-028 Digital Temperature Sensor Module: KEYES KY-028 Digital Temperature Sensor Module, used to measure changes in temperature.
